# Fritzing sketch SHADOW MSE Edition UNO Shield (saved by Fritzing 0.9.3b)
circuit board: 6.88566cm x 5.36311cm
breadboards: 1

parts:
  Motor = Dagu DGServo 9g header (male) [package=THT]
  Servo = Dagu DGServo 9g header (male) [package=THT]
  Part2 = MP3 Trigger
  MP3_Trigger = Dagu DGServo 9g header (male) [package=THT]
  Part1 = Arduino Uno (Rev3)

nets:
  GND: Motor.gnd, Servo.gnd, Part2.GND, MP3_Trigger.gnd, Part1.GND
  VCC: Motor.Vcc, Servo.Vcc, Part2.USBVCC, MP3_Trigger.Vcc, Part1.VIN
  N1: Motor.pulse, Part1.D13/SCK
  N2: Servo.pulse, Part1.D12/MISO
  N3: Part2.RX-I, MP3_Trigger.pulse, Part1.D11_PWM/MOSI

notes:
  GND
  VCC
  SIG
